# Fritzing sketch Lantern (saved by Fritzing 0.9.3b)
breadboards: 1

parts:
  Piezo_Element = Piezo Speaker
  1_Mohm = Resistor [tolerance=±5% resistance=1M package=THT]
  MCP602_Dual_Op_Amps_1 = Dual Op-Amp [package=dip08]
  R1 = Resistor [tolerance=±5% resistance=330k package=THT]
  R2 = Resistor [tolerance=±5% resistance=10k package=THT]
  D1 = Rectifier Diode [part_number=1N4001 package="300 mil [THT]"]
  C1 = Tantalum Capacitor [capacitance=1μF package="100 mil [THT, tantalum]"]
  R3 = Resistor [tolerance=±5% resistance=470k package=THT]
  MCP602_Dual_Op_Amps_2 = Dual Op-Amp [package=dip08]
  R4 = Resistor [tolerance=±5% resistance=100 package=THT]
  R5 = Resistor [tolerance=±5% resistance=560 package=THT]
  R6 = Resistor [tolerance=±5% resistance=100 package=THT]
  R7 = Resistor [tolerance=±5% resistance=18 package=THT]

nets:
  GND: Piezo_Element.pin1, 1_Mohm.Pin_0, MCP602_Dual_Op_Amps_1.A_V+, R2.Pin_0, C1.-, R3.Pin_1, MCP602_Dual_Op_Amps_2.A_V+, R7.Pin_1
  NonInv Amp (33x): Piezo_Element.pin2, 1_Mohm.Pin_1, MCP602_Dual_Op_Amps_1.A_+IN
  N1: MCP602_Dual_Op_Amps_1.A_OUT, R1.Pin_0, D1.anode
  N2: MCP602_Dual_Op_Amps_1.A_-IN, R1.Pin_1, R2.Pin_1
  5V: MCP602_Dual_Op_Amps_1.A_V-, MCP602_Dual_Op_Amps_2.A_V-, R6.Pin_0
  Percussive Envelope Detector: MCP602_Dual_Op_Amps_1.B_+IN, D1.cathode, C1.+, R3.Pin_0
  Buffer: MCP602_Dual_Op_Amps_1.B_-IN, MCP602_Dual_Op_Amps_1.B_OUT, R4.Pin_0
  SIG Out: MCP602_Dual_Op_Amps_2.A_OUT, R5.Pin_1
  ~0.8 V Ref: MCP602_Dual_Op_Amps_2.A_-IN, R6.Pin_1, R7.Pin_0
  Schmitt Trigger Comparator: MCP602_Dual_Op_Amps_2.A_+IN, R4.Pin_1, R5.Pin_0
